# Fritzing sketch ROBOT (saved by Fritzing 0.8.7b)
breadboards: 1

parts:
  Part1 = Arduino Mega 2560 (Rev3)
  M1 = DC Motor  # not connected
  VCC1 = Battery block 9V
  J1 = Basic Servo
  J2 = Basic Servo
  M6 = Stepper Motor - Unipolar  # not connected
  VCC2 = Battery block 9V
  IC3 = l298n [chip_label=IC package="DIP (Dual Inline) [THT]"]
  M2 = DC Motor

nets:
  GND: Part1.GND, J1.gnd, J2.gnd
  VCC: Part1.5V, J1.vcc, J2.vcc
  N1: Part1.VIN, VCC2.+
  N2: Part1.D33, J1.pulse
  N3: Part1.D34, J2.pulse
  GND_2: VCC1.-, VCC2.-
  N4: IC3.IN2, M2.pin_2

custom parts:
  l298n: A DIP stand-in part for whatever IC you want. With 8 pins on a 300mil dual inline package (DIP) footprint.
